# Fritzing sketch esp8266-ds18b20-temp-sensor-circuit-diagram (saved by Fritzing 0.9.3b)
breadboards: 1

parts:
  DS1 = DS18B20 1-Wire Temperature Sensor [part_number=DS18B20]
  R1 = Resistor [tolerance=±5% resistance=4.7k package=THT]
  WeMos_D1_Mini1 = WeMos D1 Mini

nets:
  N1: DS1.GND, WeMos_D1_Mini1.G
  N2: DS1.DQ, R1.Pin_0, WeMos_D1_Mini1.D3
  VDD: DS1.VDD, R1.Pin_1, WeMos_D1_Mini1.3V3
